# Fritzing sketch pumps (saved by Fritzing 0.9.2b)

parts:
  C1 = Ceramic Capacitor [capacitance=100n package="200 mil [THT, multilayer]"]
  Q1 = PNP-Transistor [part_number=BC557C package="TO92 [THT]"]
  U4 = V_REG_LD1117VXX [package=78xxl]
  C4 = Ceramic Capacitor [capacitance=100n package="200 mil [THT, multilayer]"]
  ESP8266-1 = ESP8266-12 [part_number=ESP8266-12]
  D3 = Rectifier Diode [part_number=1N4001 package="300 mil [THT]"]
  LED1 = LED - 3mm [color="Yellow (595nm)" package="3 mm [THT]"]
  R24 = Resistor [tolerance=±5% resistance=10k package="0603 [SMD]"]
  R25 = Resistor [tolerance=±5% resistance=10k package="0603 [SMD]"]
  R26 = Resistor [tolerance=±5% resistance=1k package="0603 [SMD]"]
  R27 = Resistor [tolerance=±5% resistance=66 package="0603 [SMD]"]
  C5 = Capacitor Polarized [package=cpol-radial-100uf-25v]
  Supply = screw terminal, 3 pins
  P1 = screw terminal, 3 pins
  RESET = Momentary Switch [package=ksa_sealed_tac_switch]
  PROG = Momentary Switch [package=ksa_sealed_tac_switch]
  R23 = Resistor [tolerance=±5% resistance=10k package=THT]
  LED2 = LED - 3mm [color="Yellow (595nm)" package="3 mm [THT]"]
  R28 = Resistor [tolerance=±5% resistance=66 package="0603 [SMD]"]
  R29 = Resistor [tolerance=±5% resistance=1k package="0603 [SMD]"]
  R30 = Resistor [tolerance=±5% resistance=10k package="0603 [SMD]"]
  P2 = screw terminal, 3 pins
  D4 = Rectifier Diode [part_number=1N4001 package="300 mil [THT]"]
  C6 = Ceramic Capacitor [capacitance=100n package="200 mil [THT, multilayer]"]
  Q2 = PNP-Transistor [part_number=BC557C package="TO92 [THT]"]
  LED3 = LED - 3mm [color="Yellow (595nm)" package="3 mm [THT]"]
  R31 = Resistor [tolerance=±5% resistance=66 package="0603 [SMD]"]
  R32 = Resistor [tolerance=±5% resistance=1k package="0603 [SMD]"]
  R33 = Resistor [tolerance=±5% resistance=10k package="0603 [SMD]"]
  P3 = screw terminal, 3 pins
  D5 = Rectifier Diode [part_number=1N4001 package="300 mil [THT]"]
  C7 = Ceramic Capacitor [capacitance=100n package="200 mil [THT, multilayer]"]
  Q3 = PNP-Transistor [part_number=BC557C package="TO92 [THT]"]
  K1 = Relay 2 x switch [part_number=351 package=THT]
  K2 = Relay 2 x switch [part_number=351 package=THT]
  K3 = Relay 2 x switch [part_number=351 package=THT]
  FTL = male pin header, 3 pins [form="♂ (male)"]
  DHT11 = male pin header, 3 pins [form="♂ (male)"]
  R34 = Resistor [tolerance=±5% resistance=10k package=THT]
  Level = SWITCH-MOMENTARY-2 [package=tactile-pth-12mm]

nets:
  N1: C1.0, ESP8266-1.GPIO5, R25.Pin_1, R26.Pin_1
  N2: C1.1, Q1.B, R26.Pin_0
  N3: Q1.E, U4.OUT, ESP8266-1.VCC, R24.Pin_0, R25.Pin_0, C5.+, R23.Pin_0, R30.Pin_0, Q2.E, R33.Pin_0, Q3.E, DHT11.pin1, R34.Pin_0, Level.1
  N4: Q1.C, D3.cathode, R27.Pin_0, K1.pin_1
  GND: U4.GND, ESP8266-1.GND, D3.anode, LED1.cathode, C5.-, Supply.pin1, P1.pin1, RESET.3, RESET.4, PROG.3, PROG.4, LED2.cathode, P2.pin1, D4.anode, LED3.cathode, P3.pin1, D5.anode, K1.pin_16, K2.pin_16, K3.pin_16, FTL.pin3, DHT11.pin3, Level.2
  N5: U4.IN, C4.0, Supply.pin3, K1.pin_4, K2.pin_4, K3.pin_4
  N6: ESP8266-1.REST, RESET.1, RESET.2, R23.Pin_1
  N7: ESP8266-1.GPIO12, DHT11.pin2
  N8: ESP8266-1.GPIO13, R34.Pin_1
  N9: ESP8266-1.TXD, FTL.pin1
  N10: ESP8266-1.RXD, FTL.pin2
  N11: ESP8266-1.GPIO0, R24.Pin_1, PROG.1, PROG.2
  N12: LED1.anode, R27.Pin_1
  N13: P1.pin3, K1.pin_8
  N14: LED2.anode, R28.Pin_1
  N15: R28.Pin_0, D4.cathode, Q2.C, K2.pin_1
  N16: R29.Pin_0, C6.1, Q2.B
  N17: R29.Pin_1, R30.Pin_1, C6.0
  N18: P2.pin3, K2.pin_8
  N19: LED3.anode, R31.Pin_1
  N20: R31.Pin_0, D5.cathode, Q3.C, K3.pin_1
  N21: R32.Pin_0, C7.1, Q3.B
  N22: R32.Pin_1, R33.Pin_1, C7.0
  N23: P3.pin3, K3.pin_8

custom parts:
  Relay 2 x switch: An DPDT relay. 2 x switch, same footprint as Finder 30.22.7.005.0010 30 Series - Submimiature DIL Relays 1.25 A
