# Fritzing sketch sensor (saved by Fritzing 0.9.2b)
stripboards: 1

parts:
  ESP8266_ESP12_EPG1 = ESP8266 WiFi Module [part_number=ESP8266-ESP12]
  D1 = Schottky Diode [package="300 mil [THT]"]
  D2 = Zener Diode [breakdown_voltage=3.9V package="300 mil [THT]"]
  R2 = Resistor [tolerance=±5% resistance=4.8k package=THT]
  R3 = Resistor [tolerance=±5% resistance=2.4k package=THT]
  R6 = Resistor [tolerance=±5% resistance=1k package=THT]
  R5 = Resistor [tolerance=±5% resistance=10k package=THT]
  R7 = Resistor [tolerance=±5% resistance=66 package=THT]
  3xAA_NIMH = male pin header, 2 pins [form="♂ (male)"]
  SOLAR = male pin header, 2 pins [form="♂ (male)"]
  left = female pin header, 8 pins [form="♀ (female)"]
  right = female pin header, 8 pins [form="♀ (female)"]
  SOIL = female pin header, 4 pins [form="♀ (female)"]
  DHT11 = male pin header, 3 pins [form="♂ (male)"]
  C1 = Ceramic Capacitor [capacitance=100n package="200 mil [THT, multilayer]"]
  Q1 = PNP-Transistor [package="TO92 [THT]"]

nets:
  N1: ESP8266_ESP12_EPG1.VCC, D1.cathode, R5.Pin_0, R7.Pin_0, 3xAA_NIMH.pin1, left.pin8, Q1.E
  N2: ESP8266_ESP12_EPG1.CH_PD, left.pin4
  N3: ESP8266_ESP12_EPG1.GND, D2.anode, R3.Pin_1, 3xAA_NIMH.pin2, SOLAR.pin2, right.pin8, SOIL.pin2, DHT11.pin3
  N4: ESP8266_ESP12_EPG1.GPIO_5, R6.Pin_1, R5.Pin_1, right.pin4, C1.0
  N5: ESP8266_ESP12_EPG1.ADC_0, R2.Pin_1, R3.Pin_0, left.pin2
  N6: ESP8266_ESP12_EPG1.GPIO_13, left.pin7, DHT11.pin1
  N7: D1.anode, SOLAR.pin1
  N8: D2.cathode, R7.Pin_1
  N9: R2.Pin_0, SOIL.pin4
  N10: R6.Pin_0, C1.1, Q1.B
  N11: SOIL.pin1, DHT11.pin2, Q1.C

custom parts:
  ESP8266 WiFi Module: Mini ESP8266 Breakout Board
